// Logisim project assignment2.circ as structural Verilog: 1 circuit, main circuit main
module main (
  input  [1:0] Address,
  input  [3:0] Data,
  input  in_3,
  output [3:0] Output,
  output [3:0] out_5,
  output [3:0] out_6,
  output [3:0] out_7,
  output [3:0] out_8
);

  wire and_1_out, and_2_out, and_3_out, and_4_out, and_5_out, and_6_out, and_7_out, and_8_out, and_9_out,
       and_10_out, and_11_out, and_12_out, and_13_out, and_14_out, and_15_out, and_16_out, and_17_out,
       and_18_out, and_19_out, and_20_out, and_21_out, and_22_out, and_23_out, and_24_out, and_25_out,
       and_26_out, and_27_out, and_28_out, and_29_out, and_30_out, and_31_out, and_32_out, and_33_out,
       and_34_out, and_35_out, and_36_out, and_37_out, and_38_out, and_39_out, and_40_out, and_41_out,
       and_42_out, and_43_out, and_44_out, and_45_out, and_46_out, and_47_out, and_48_out, and_49_out,
       and_50_out, and_51_out, and_52_out, clock_1_out, not_1_out, not_2_out, not_3_out, not_4_out,
       not_5_out, not_6_out, not_7_out, not_8_out, not_9_out, not_10_out, not_11_out, not_12_out, not_13_out,
       not_14_out, not_15_out, not_16_out, not_17_out, not_18_out, not_19_out, not_20_out, or_1_out,
       or_2_out, or_3_out, or_4_out, or_5_out, or_6_out, or_7_out, or_8_out, or_9_out, or_10_out, or_11_out,
       or_12_out, or_13_out, or_14_out, or_15_out, or_16_out;

  not not_1 (not_1_out, Address[1]);
  not not_2 (not_2_out, Address[0]);
  not not_3 (not_3_out, Address[0]);
  not not_4 (not_4_out, Address[1]);
  and and_1 (and_1_out, not_1_out, not_2_out);
  and and_2 (and_2_out, Address[1], not_3_out);
  and and_3 (and_3_out, not_4_out, Address[0]);
  and and_4 (and_4_out, Address[1], Address[0]);
  Clock clock_1 (.out(clock_1_out));
  and and_5 (and_5_out, in_3, clock_1_out, and_1_out);
  D_Flip_Flop d_ff_1 (.clk(and_5_out), .D(Data[0]), .Q(out_5[0]));  // open: Qn, preset, en, reset
  and and_6 (and_6_out, in_3, clock_1_out, and_1_out);
  D_Flip_Flop d_ff_2 (.clk(and_6_out), .D(Data[1]), .Q(out_5[1]));  // open: Qn, preset, en, reset
  D_Flip_Flop d_ff_3 (.clk(and_7_out), .D(Data[2]), .Q(out_5[2]));  // open: Qn, preset, en, reset
  and and_7 (and_7_out, in_3, clock_1_out, and_1_out);
  D_Flip_Flop d_ff_4 (.clk(and_8_out), .D(Data[3]), .Q(out_5[3]));  // open: Qn, preset, en, reset
  and and_8 (and_8_out, in_3, clock_1_out, and_1_out);
  D_Flip_Flop d_ff_5 (.clk(and_9_out), .D(Data[0]), .Q(out_6[0]));  // open: Qn, preset, en, reset
  and and_9 (and_9_out, in_3, clock_1_out, and_2_out);
  D_Flip_Flop d_ff_6 (.clk(and_10_out), .D(Data[1]), .Q(out_6[1]));  // open: Qn, preset, en, reset
  and and_10 (and_10_out, in_3, clock_1_out, and_2_out);
  and and_11 (and_11_out, in_3, clock_1_out, and_2_out);
  D_Flip_Flop d_ff_7 (.clk(and_11_out), .D(Data[2]), .Q(out_6[2]));  // open: Qn, preset, en, reset
  and and_12 (and_12_out, in_3, clock_1_out, and_2_out);
  D_Flip_Flop d_ff_8 (.clk(and_12_out), .D(Data[3]), .Q(out_6[3]));  // open: Qn, preset, en, reset
  and and_13 (and_13_out, in_3, clock_1_out, and_3_out);
  and and_14 (and_14_out, in_3, clock_1_out, and_3_out);
  and and_15 (and_15_out, in_3, clock_1_out, and_3_out);
  and and_16 (and_16_out, in_3, clock_1_out, and_3_out);
  D_Flip_Flop d_ff_9 (.clk(and_13_out), .D(Data[0]), .Q(out_7[0]));  // open: Qn, preset, en, reset
  D_Flip_Flop d_ff_10 (.clk(and_14_out), .D(Data[1]), .Q(out_7[1]));  // open: Qn, preset, en, reset
  D_Flip_Flop d_ff_11 (.clk(and_15_out), .D(Data[2]), .Q(out_7[2]));  // open: Qn, preset, en, reset
  D_Flip_Flop d_ff_12 (.clk(and_16_out), .D(Data[3]), .Q(out_7[3]));  // open: Qn, preset, en, reset
  and and_17 (and_17_out, in_3, clock_1_out, and_4_out);
  and and_18 (and_18_out, in_3, clock_1_out, and_4_out);
  and and_19 (and_19_out, in_3, clock_1_out, and_4_out);
  and and_20 (and_20_out, in_3, clock_1_out, and_4_out);
  D_Flip_Flop d_ff_13 (.clk(and_17_out), .D(Data[0]), .Q(out_8[0]));  // open: Qn, preset, en, reset
  D_Flip_Flop d_ff_14 (.clk(and_18_out), .D(Data[1]), .Q(out_8[1]));  // open: Qn, preset, en, reset
  D_Flip_Flop d_ff_15 (.clk(and_19_out), .D(Data[2]), .Q(out_8[2]));  // open: Qn, preset, en, reset
  D_Flip_Flop d_ff_16 (.clk(and_20_out), .D(Data[3]), .Q(out_8[3]));  // open: Qn, preset, en, reset
  not not_5 (not_5_out, in_3);
  not not_6 (not_6_out, in_3);
  not not_7 (not_7_out, in_3);
  not not_8 (not_8_out, in_3);
  not not_9 (not_9_out, in_3);
  not not_10 (not_10_out, in_3);
  not not_11 (not_11_out, in_3);
  not not_12 (not_12_out, in_3);
  not not_13 (not_13_out, in_3);
  not not_14 (not_14_out, in_3);
  not not_15 (not_15_out, in_3);
  not not_16 (not_16_out, in_3);
  not not_17 (not_17_out, in_3);
  not not_18 (not_18_out, in_3);
  not not_19 (not_19_out, in_3);
  not not_20 (not_20_out, in_3);
  and and_21 (and_21_out, in_3, clock_1_out, and_1_out, Data[0]);
  or or_1 (or_1_out, and_21_out, and_22_out);
  and and_22 (and_22_out, not_5_out, clock_1_out, and_1_out, out_5[0]);
  and and_23 (and_23_out, in_3, clock_1_out, and_2_out, Data[0]);
  or or_2 (or_2_out, and_23_out, and_24_out);
  and and_24 (and_24_out, not_6_out, clock_1_out, and_2_out, out_6[0]);
  and and_25 (and_25_out, in_3, clock_1_out, and_3_out, Data[0]);
  or or_3 (or_3_out, and_25_out, and_26_out);
  and and_26 (and_26_out, not_7_out, clock_1_out, and_3_out, out_7[0]);
  and and_27 (and_27_out, in_3, clock_1_out, and_4_out, Data[0]);
  or or_4 (or_4_out, and_27_out, and_28_out);
  and and_28 (and_28_out, not_8_out, clock_1_out, and_4_out, out_8[0]);
  and and_29 (and_29_out, in_3, clock_1_out, and_1_out, Data[1]);
  or or_5 (or_5_out, and_29_out, and_30_out);
  and and_30 (and_30_out, not_9_out, clock_1_out, and_1_out, out_5[1]);
  and and_31 (and_31_out, in_3, clock_1_out, and_2_out, Data[1]);
  or or_6 (or_6_out, and_31_out, and_32_out);
  and and_32 (and_32_out, not_10_out, clock_1_out, and_2_out, out_6[1]);
  and and_33 (and_33_out, in_3, clock_1_out, and_3_out, Data[1]);
  or or_7 (or_7_out, and_33_out, and_34_out);
  and and_34 (and_34_out, not_11_out, clock_1_out, and_3_out, out_7[1]);
  and and_35 (and_35_out, in_3, clock_1_out, and_4_out, Data[1]);
  or or_8 (or_8_out, and_35_out, and_36_out);
  and and_36 (and_36_out, not_12_out, clock_1_out, and_4_out, out_8[1]);
  and and_37 (and_37_out, in_3, clock_1_out, and_1_out, Data[2]);
  or or_9 (or_9_out, and_37_out, and_38_out);
  and and_38 (and_38_out, not_13_out, clock_1_out, and_1_out, out_5[2]);
  and and_39 (and_39_out, in_3, clock_1_out, and_2_out, Data[2]);
  or or_10 (or_10_out, and_39_out, and_40_out);
  and and_40 (and_40_out, not_14_out, clock_1_out, and_2_out, out_6[2]);
  and and_41 (and_41_out, in_3, clock_1_out, and_3_out, Data[2]);
  or or_11 (or_11_out, and_41_out, and_42_out);
  and and_42 (and_42_out, not_15_out, clock_1_out, and_3_out, out_7[2]);
  and and_43 (and_43_out, in_3, clock_1_out, and_4_out, Data[2]);
  or or_12 (or_12_out, and_43_out, and_44_out);
  and and_44 (and_44_out, not_16_out, clock_1_out, and_4_out, out_8[2]);
  and and_45 (and_45_out, in_3, clock_1_out, and_1_out, Data[3]);
  or or_13 (or_13_out, and_45_out, and_46_out);
  and and_46 (and_46_out, not_17_out, clock_1_out, and_1_out, out_5[3]);
  and and_47 (and_47_out, in_3, clock_1_out, and_2_out, Data[3]);
  or or_14 (or_14_out, and_47_out, and_48_out);
  and and_48 (and_48_out, not_18_out, clock_1_out, and_2_out, out_6[3]);
  and and_49 (and_49_out, in_3, clock_1_out, and_3_out, Data[3]);
  or or_15 (or_15_out, and_49_out, and_50_out);
  and and_50 (and_50_out, not_19_out, clock_1_out, and_3_out, out_7[3]);
  and and_51 (and_51_out, in_3, clock_1_out, and_4_out, Data[3]);
  or or_16 (or_16_out, and_51_out, and_52_out);
  and and_52 (and_52_out, not_20_out, clock_1_out, and_4_out, out_8[3]);
  or or_17 (Output[0], or_1_out, or_2_out, or_3_out, or_4_out);
  or or_18 (Output[1], or_5_out, or_6_out, or_7_out, or_8_out);
  or or_19 (Output[2], or_9_out, or_10_out, or_11_out, or_12_out);
  or or_20 (Output[3], or_13_out, or_14_out, or_15_out, or_16_out);

  // Notes on the sheet:
  //   Mode (1=write,0=read)
  //   Clock
  //   DO NOT MOVE the inputs, outputs or clock, Anything else can be moved.
  //   Mode Clock
  //   address
  //   U-bus
  //   output bit 0 
  //   output bit 1
  //   output bit 2
  //   output bit 3 
endmodule
