// Logisim project assignment3.circ as structural Verilog: 3 circuits, main circuit main
module main (
  input  [3:0] in_1,
  input  [3:0] in_2,
  input  _0_add_1_sub,
  output [3:0] out_4,
  output [3:0] out_5,
  output [3:0] out_6,
  output [3:0] out_7
);

  wire clock_1_out;
  wire [3:0] alu_1_a_out, alu_1_status;

  Clock clock_1 (.out(clock_1_out));
  Register #(.width(4)) L (.D(in_1), .Q(out_4), .clk(clock_1_out));  // open: en, clr
  ALU alu_1 (._0_add_1_sub(_0_add_1_sub), .R(out_5), .L(out_4), .Status(alu_1_status), .A_out(alu_1_a_out));
  Register #(.width(4)) R (.D(in_2), .Q(out_5), .clk(clock_1_out));  // open: en, clr
  Register #(.width(4), .trigger("high")) A_out (.D(alu_1_a_out), .Q(out_6), .clk(clock_1_out));  // open: en, clr
  Register #(.width(4), .trigger("high")) status (.D(alu_1_status), .Q(out_7), .clk(clock_1_out));  // open: en, clr
endmodule

module ALU (
  input  _0_add_1_sub,
  input  [3:0] R,
  input  [3:0] L,
  output [3:0] Status,
  output [3:0] A_out
);

  wire _0_2_out, _0_3_out, _0_out, _1_2_out, _1_3_out, _1_out, _2_2_out, _2_3_out, _2_out,
       _2_s_complement_output_0, _2_s_complement_output_1, _2_s_complement_output_2,
       _2_s_complement_output_3, _3_2_out, _3_3_out, _3_out, adder_1_cout, adder_2_cout, adder_3_cout,
       and_1_out, and_2_out;

  and _2 (_2_out, ~_0_add_1_sub, R[2]);  // AND_Gate
  and _1 (_1_out, ~_0_add_1_sub, R[1]);  // AND_Gate
  and _3 (_3_out, ~_0_add_1_sub, R[3]);  // AND_Gate
  or _2_2 (_2_2_out, _2_out, _2_s_complement_output_2);
  or _3_2 (_3_2_out, _3_out, _2_s_complement_output_3);
  or _1_2 (_1_2_out, _1_out, _2_s_complement_output_1);
  and _3_3 (_3_3_out, R[3], _0_add_1_sub);
  and _0 (_0_out, ~_0_add_1_sub, R[0]);  // AND_Gate
  or _0_2 (_0_2_out, _0_out, _2_s_complement_output_0);
  and _1_3 (_1_3_out, R[1], _0_add_1_sub);
  and _0_3 (_0_3_out, R[0], _0_add_1_sub);
  and _2_3 (_2_3_out, R[2], _0_add_1_sub);
  _2_s_complement _2_s_complement (
    .input_3(_3_3_out), .input_2(_2_3_out), .input_1(_1_3_out), .input_0(_0_3_out),
    .output_0(_2_s_complement_output_0), .output_1(_2_s_complement_output_1),
    .output_2(_2_s_complement_output_2), .output_3(_2_s_complement_output_3));
  Adder #(.width(1)) adder_1 (.a(_0_2_out), .b(L[0]), .out(A_out[0]), .cout(adder_1_cout));  // open: cin
  Adder #(.width(1)) adder_2 (.a(_1_2_out), .b(L[1]), .out(A_out[1]), .cin(adder_1_cout), .cout(adder_2_cout));
  Adder #(.width(1)) adder_3 (.a(_2_2_out), .b(L[2]), .out(A_out[2]), .cin(adder_2_cout), .cout(adder_3_cout));
  Adder #(.width(1)) adder_4 (.a(_3_2_out), .b(L[3]), .out(A_out[3]), .cin(adder_3_cout), .cout(Status[0]));
  and and_1 (and_1_out, _3_2_out, L[3], ~A_out[3]);  // AND_Gate
  and and_2 (and_2_out, ~_3_2_out, ~L[3], A_out[3]);  // AND_Gate
  or or_1 (Status[1], and_1_out, and_2_out);
  and and_3 (Status[2], ~A_out[0], ~A_out[1], ~A_out[2], ~A_out[3]);  // AND_Gate

  assign Status[3] = A_out[3];

  // Notes on the sheet:
  //   R3
  //   L3
  //   A3
endmodule

module _2_s_complement (
  input  input_3,
  input  input_2,
  input  input_1,
  input  input_0,
  output output_0,
  output output_1,
  output output_2,
  output output_3
);

  wire adder_2_cout, adder_3_cout, adder_4_cout, not_1_out, not_2_out, not_3_out, not_4_out;

  not not_1 (not_1_out, input_3);
  not not_2 (not_2_out, input_2);
  not not_3 (not_3_out, input_1);
  Adder #(.width(1)) adder_1 (.a(adder_4_cout), .b(not_1_out), .out(output_3));  // open: cin, cout
  not not_4 (not_4_out, input_0);
  Adder #(.width(1)) adder_2 (.a(1'b1), .b(not_4_out), .out(output_0), .cout(adder_2_cout));  // open: cin
  Adder #(.width(1)) adder_3 (.a(adder_2_cout), .b(not_3_out), .out(output_1), .cout(adder_3_cout));  // open: cin
  Adder #(.width(1)) adder_4 (.a(adder_3_cout), .b(not_2_out), .out(output_2), .cout(adder_4_cout));  // open: cin
endmodule
