// Logisim project assignment4.circ as structural Verilog: 7 circuits, main circuit main
module main (
  input  [7:0] Initialization_data,
  input  _1_for_initialization,
  input  [1:0] Address,
  input  _0_move_1merge,
  input  [1:0] R1,
  input  [1:0] R2,
  input  [1:0] R3
);

  wire and_1_out, and_2_out, and_3_out, clock_1_out, cu_1_give_a_write, cu_1_last_step_trigger,
       cu_1_need_a_read, initialization_box_1_ra, initialization_box_1_rb, initialization_box_1_rc, OP_q,
       or_1_out, or_2_out, or_3_out;
  wire [1:0] incrementor_1_step_counter, STEP_q;
  wire [3:0] Rb_01_q, Rc_10_q, write_selector_8_bits_2_output_2, write_selector_8_bits_3_output_2;
  wire [6:0] IR_q;
  wire [7:0] cu_1_write_data, Ra_00_q, read_selctor_8bits_1_read1, read_selctor_8bits_1_read2,
       write_selector_8_bits_1_output;
  wire [7:4] write_selector_8_bits_2_output, write_selector_8_bits_3_output;

  Clock clock_1 (.out(clock_1_out));
  Register #(.width(7)) IR (.D({_0_move_1merge, R1, R2, R3}), .Q(IR_q), .clk(clock_1_out));  // open: en, clr
  Register #(.width(1), .trigger("high")) OP (.D(IR_q[6]), .Q(OP_q), .clk(clock_1_out));  // open: en, clr
  Register #(.width(2)) STEP (.D(incrementor_1_step_counter), .Q(STEP_q), .clk(clock_1_out));  // open: en, clr
  // Probe on IR_q
  CU cu_1 (
    .Read1(read_selctor_8bits_1_read1), .Read2(read_selctor_8bits_1_read2), .OP(OP_q), .STEP(STEP_q),
    .Need_A_Read(cu_1_need_a_read), .Give_a_Write(cu_1_give_a_write),
    .Last_Step_Trigger(cu_1_last_step_trigger), .Write_Data(cu_1_write_data));
  Incrementor incrementor_1 (
    .CLock(clock_1_out), .Last_Step_Trigger(cu_1_last_step_trigger), .STEP_Counter(incrementor_1_step_counter));
  // Probe on IR_q[5:4]
  Initialization_box initialization_box_1 (
    ._1_for_initialization(_1_for_initialization), .Address(Address), .Ra(initialization_box_1_ra),
    .Rb(initialization_box_1_rb), .Rc(initialization_box_1_rc));
  and and_1 (and_1_out, ~IR_q[5], ~IR_q[4], cu_1_give_a_write, clock_1_out);  // AND_Gate
  and and_2 (and_2_out, ~IR_q[5], IR_q[4], cu_1_give_a_write, clock_1_out);  // AND_Gate
  and and_3 (and_3_out, IR_q[5], ~IR_q[4], cu_1_give_a_write, clock_1_out);  // AND_Gate
  Write_Selector_8_bits write_selector_8_bits_1 (
    .Regular_Data_bus(cu_1_write_data), .Initialization_Data(Initialization_data),
    ._1_Initialization(_1_for_initialization), .Output(write_selector_8_bits_1_output));
  Write_Selector_8_bits write_selector_8_bits_2 (
    .Regular_Data_bus(cu_1_write_data), .Initialization_Data(Initialization_data),
    ._1_Initialization(_1_for_initialization),
    .Output({write_selector_8_bits_2_output, write_selector_8_bits_2_output_2}));
  Write_Selector_8_bits write_selector_8_bits_3 (
    .Regular_Data_bus(cu_1_write_data), .Initialization_Data(Initialization_data),
    ._1_Initialization(_1_for_initialization),
    .Output({write_selector_8_bits_3_output, write_selector_8_bits_3_output_2}));
  or or_1 (or_1_out, initialization_box_1_ra, and_1_out);
  or or_2 (or_2_out, and_2_out, initialization_box_1_rb);
  or or_3 (or_3_out, initialization_box_1_rc, and_3_out);
  Register #(.trigger("high")) Ra_00 (
    .D(write_selector_8_bits_1_output), .Q(Ra_00_q), .clk(or_1_out));  // open: en, clr
  Register #(.width(4), .trigger("high")) Rb_01 (
    .D(write_selector_8_bits_2_output_2), .Q(Rb_01_q), .clk(or_2_out));  // open: en, clr
  // Probe on Rc_10_q
  Register #(.width(4), .trigger("high")) Rc_10 (
    .D(write_selector_8_bits_3_output_2), .Q(Rc_10_q), .clk(or_3_out));  // open: en, clr
  // Probe on Ra_00_q
  // Probe on Rb_01_q
  Read_Selctor_8bits read_selctor_8bits_1 (
    .Need_A_Read(cu_1_need_a_read), .OP(IR_q[6]), .Ra(Ra_00_q), .Rb(Rb_01_q), .Rc(Rc_10_q), .R1(IR_q[5:4]),
    .R2(IR_q[3:2]), .R3(IR_q[1:0]), .Read1(read_selctor_8bits_1_read1), .Read2(read_selctor_8bits_1_read2));
  // Probe on read_selctor_8bits_1_read1
  // Probe on read_selctor_8bits_1_read2

  // Notes on the sheet:
  //   move 2 ticks merge 4 ticks
endmodule

module CU (
  input  [7:0] Read1,
  input  [7:0] Read2,
  input  OP,
  input  [1:0] STEP,
  output Need_A_Read,
  output Give_a_Write,
  output Last_Step_Trigger,
  output [7:0] Write_Data
);

  wire and_1_out, and_3_out, and_4_out, not_1_out, or_1_out;
  wire [3:0] and_8_out;
  wire [7:0] and_7_out, and_9_out, and_10_out, Merge_q, T1_q, T2_q;
  wire [7:4] and_8_out_2;
  wire [7:7] and_2_out, and_5_out, and_6_out;

  not not_1 (not_1_out, OP);
  and and_1 (and_1_out, not_1_out, ~STEP[0], ~STEP[1]);  // AND_Gate
  and and_2 (and_2_out[7], not_1_out, STEP[0], ~STEP[1]);  // AND_Gate
  and and_3 (and_3_out, OP, ~STEP[0], ~STEP[1]);  // AND_Gate
  and and_4 (and_4_out, OP, STEP[0], ~STEP[1]);  // AND_Gate
  and and_5 (and_5_out[7], OP, ~STEP[0], STEP[1]);  // AND_Gate
  and and_6 (and_6_out[7], OP, STEP[0], STEP[1]);
  assign and_7_out = {8{and_5_out[7]}} & T1_q;  // AND_Gate and_7, 8 bits wide
  Subtractor subtractor_1 ();  // open: a, b, out, bin, bout
  Register #(.trigger("high")) T1 (.D(Read1), .Q(T1_q), .clk(or_1_out));  // open: en, clr
  or or_1 (or_1_out, and_1_out, and_3_out);
  assign {and_8_out_2, and_8_out} = {8{and_5_out[7]}} & T2_q;  // AND_Gate and_8, 8 bits wide
  Register #(.trigger("high")) T2 (.D(Read2), .Q(T2_q), .clk(and_4_out));  // open: en, clr
  Register #(.trigger("high")) Merge (
    .D({and_7_out[7:4], and_8_out}), .Q(Merge_q), .clk(and_5_out[7]));  // open: en, clr
  assign and_9_out = {8{and_2_out[7]}} & T1_q;  // AND_Gate and_9, 8 bits wide
  assign Write_Data = and_9_out | and_10_out;  // OR_Gate or_2, 8 bits wide
  assign and_10_out = {8{and_6_out[7]}} & Merge_q;  // AND_Gate and_10, 8 bits wide
  or or_3 (Need_A_Read, and_1_out, and_3_out, and_4_out);
  or or_4 (Give_a_Write, and_2_out[7], and_6_out[7]);
  or or_5 (Last_Step_Trigger, and_2_out[7], and_6_out[7]);

  // Notes on the sheet:
  //   Micro Step Move(0)1.LB 2.SB 
  //   Micro Step Merge(1) 1. LB 2.LB 3.Merge 4. SB
endmodule

module Incrementor (
  input  CLock,
  input  Last_Step_Trigger,
  output [1:0] STEP_Counter
);

  wire [1:0] adder_1_out, and_1_out, and_2_out, not_1_out, or_1_out;

  assign not_1_out = ~{2{Last_Step_Trigger}};  // NOT_Gate not_1, 2 bits wide
  assign and_1_out = {2{Last_Step_Trigger}} & 2'b00;  // AND_Gate and_1, 2 bits wide
  assign and_2_out = not_1_out & adder_1_out;  // AND_Gate and_2, 2 bits wide
  assign or_1_out = and_1_out | and_2_out;  // OR_Gate or_1, 2 bits wide
  Register #(.width(2), .trigger("falling")) STEP (.D(or_1_out), .Q(STEP_Counter), .clk(CLock));  // open: en, clr
  Adder #(.width(2)) adder_1 (.a(STEP_Counter), .b(2'b01), .out(adder_1_out));  // open: cin, cout
endmodule

module Initialization_box (
  input  _1_for_initialization,
  input  [1:0] Address,
  output Ra,
  output Rb,
  output Rc
);

  and and_1 (Ra, ~Address[0], ~Address[1], _1_for_initialization);  // AND_Gate
  and and_2 (Rb, ~Address[1], Address[0], _1_for_initialization);  // AND_Gate
  and and_3 (Rc, Address[1], ~Address[0], _1_for_initialization);  // AND_Gate
endmodule

module Write_Selector_8_bits (
  input  [7:0] Regular_Data_bus,
  input  [7:0] Initialization_Data,
  input  _1_Initialization,
  output [7:0] Output
);

  wire [7:0] and_1_out, and_2_out;

  assign and_1_out = ~{8{_1_Initialization}} & Regular_Data_bus;  // AND_Gate and_1, 8 bits wide
  // Probe on and_1_out
  assign and_2_out = {8{_1_Initialization}} & Initialization_Data;  // AND_Gate and_2, 8 bits wide
  // Probe on and_2_out
  assign Output = and_1_out | and_2_out;  // OR_Gate or_1, 8 bits wide
endmodule

module Read_Selctor_8bits (
  input  Need_A_Read,
  input  OP,
  input  [7:0] Ra,
  input  [3:0] Rb,
  input  [3:0] Rc,
  input  [1:0] R1,
  input  [1:0] R2,
  input  [1:0] R3,
  output [7:0] Read1,
  output [7:0] Read2
);

  wire and_22_out, not_1_out, or_1_out;
  wire [1:0] subtractor_1_out;
  wire [7:0] and_17_out, and_18_out, and_23_out, and_24_out, and_25_out, and_26_out, and_27_out, and_28_out,
       and_29_out, and_30_out, and_31_out, and_32_out, and_33_out, and_34_out, and_35_out, and_36_out,
       and_37_out, and_38_out, and_39_out, and_40_out, and_41_out, and_42_out, and_43_out, and_44_out,
       and_45_out, and_46_out, and_47_out, and_48_out, or_2_out, read_selector_2_1_read1,
       read_selector_2_1_read2;
  wire [7:7] and_1_out, and_2_out, and_3_out, and_4_out, and_5_out, and_6_out, and_7_out, and_8_out,
       and_9_out, and_10_out, and_11_out, and_12_out, and_13_out, and_14_out, and_15_out, and_16_out,
       and_19_out, and_20_out, and_21_out;

  Subtractor #(.width(2)) subtractor_1 (.a(R1), .b(R2), .out(subtractor_1_out));  // open: bin, bout
  or or_1 (or_1_out, R1[0], R1[1]);
  and and_1 (and_1_out[7], Need_A_Read, ~OP, ~R1[0], ~R1[1], ~R2[1], R2[0]);  // AND_Gate
  and and_2 (and_2_out[7], Need_A_Read, ~OP, ~R1[0], ~R1[1], R2[1], ~R2[0]);  // AND_Gate
  and and_3 (and_3_out[7], Need_A_Read, ~OP, ~R1[1], R1[0], ~R2[1], ~R2[0]);  // AND_Gate
  and and_4 (and_4_out[7], Need_A_Read, ~OP, ~R1[1], R1[0], R2[1], ~R2[0]);  // AND_Gate
  and and_5 (and_5_out[7], Need_A_Read, ~OP, R1[1], ~R1[0], ~R2[1], ~R2[0]);  // AND_Gate
  and and_6 (and_6_out[7], Need_A_Read, ~OP, R1[1], ~R1[0], ~R2[1], R2[0]);  // AND_Gate
  and and_7 (and_7_out[7], Need_A_Read, OP, ~R1[1], ~R1[0], ~R2[1], R2[0], R3[1], ~R3[0]);  // AND_Gate
  and and_8 (and_8_out[7], Need_A_Read, OP, ~R1[1], ~R1[0], R2[1], ~R2[0], ~R3[1], R3[0]);  // AND_Gate
  and and_9 (and_9_out[7], Need_A_Read, ~OP, ~subtractor_1_out[0], ~subtractor_1_out[1]);  // AND_Gate
  and and_10 (and_10_out[7], Need_A_Read, Need_A_Read, ~R1[1], ~R1[0], ~R2[1], ~R2[0], ~R3[1], ~R3[0]);  // AND_Gate
  and and_11 (and_11_out[7], Need_A_Read, OP, ~R1[1], ~R1[0], ~R2[1], R2[0], ~R3[1], ~R3[0]);  // AND_Gate
  and and_12 (and_12_out[7], Need_A_Read, OP, ~R1[1], ~R1[0], ~R2[1], ~R2[0], R3[1], ~R3[0]);  // AND_Gate
  and and_13 (and_13_out[7], Need_A_Read, OP, ~R1[1], ~R1[0], R2[1], ~R2[0], ~R3[1], ~R3[0]);  // AND_Gate
  and and_14 (and_14_out[7], Need_A_Read, OP, ~R1[1], ~R1[0], ~R2[1], ~R2[0], ~R3[1], R3[0]);  // AND_Gate
  and and_15 (and_15_out[7], Need_A_Read, OP, ~R1[1], ~R1[0], ~R2[1], R2[0], ~R3[1], R3[0]);  // AND_Gate
  and and_16 (and_16_out[7], Need_A_Read, OP, ~R1[1], ~R1[0], R2[1], ~R2[0], R3[1], ~R3[0]);  // AND_Gate
  assign and_17_out = {8{and_3_out[7]}} & Ra;  // AND_Gate and_17, 8 bits wide
  assign and_18_out = {8{and_4_out[7]}} & {Rc, Rc};  // AND_Gate and_18, 8 bits wide
  and and_19 (and_19_out[7], ~R1[0], ~R1[1]);  // AND_Gate
  and and_20 (and_20_out[7], ~R1[1], R1[0]);  // AND_Gate
  and and_21 (and_21_out[7], R1[1], ~R1[0]);  // AND_Gate
  and and_22 (and_22_out, Need_A_Read, OP, or_1_out);
  // Probe on and_23_out
  assign and_23_out = {8{and_1_out[7]}} & {Ra[7:4], Rb};  // AND_Gate and_23, 8 bits wide
  // Probe on and_24_out
  assign and_24_out = {8{and_2_out[7]}} & {Ra[7:4], Rc};  // AND_Gate and_24, 8 bits wide
  // Probe on and_17_out
  // Probe on and_18_out
  // Probe on and_25_out
  assign and_25_out = {8{and_5_out[7]}} & Ra;  // AND_Gate and_25, 8 bits wide
  // Probe on and_26_out
  assign and_26_out = {8{and_6_out[7]}} & {Rb, Rb};  // AND_Gate and_26, 8 bits wide
  assign and_27_out = {8{and_7_out[7]}} & {Rc, Rc};  // AND_Gate and_27, 8 bits wide
  assign and_28_out = {8{and_19_out[7]}} & Ra;  // AND_Gate and_28, 8 bits wide
  assign and_29_out = {8{and_20_out[7]}} & {Rb, Rb};  // AND_Gate and_29, 8 bits wide
  assign and_30_out = {8{and_21_out[7]}} & {Rc, Rc};  // AND_Gate and_30, 8 bits wide
  // Probe on and_31_out
  assign and_31_out = {8{and_7_out[7]}} & {Rb, Rb};  // AND_Gate and_31, 8 bits wide
  // Probe on and_27_out
  assign and_32_out = {8{and_8_out[7]}} & {Rc, Rc};  // AND_Gate and_32, 8 bits wide
  assign and_33_out = {8{and_8_out[7]}} & {Rb, Rb};  // AND_Gate and_33, 8 bits wide
  assign and_34_out = {8{and_10_out[7]}} & Ra;  // AND_Gate and_34, 8 bits wide
  assign and_35_out = {8{and_10_out[7]}} & Ra;  // AND_Gate and_35, 8 bits wide
  assign and_36_out = {8{and_11_out[7]}} & {Rb, Rb};  // AND_Gate and_36, 8 bits wide
  assign and_37_out = {8{and_11_out[7]}} & Ra;  // AND_Gate and_37, 8 bits wide
  assign and_38_out = {8{and_12_out[7]}} & Ra;  // AND_Gate and_38, 8 bits wide
  assign and_39_out = {8{and_12_out[7]}} & {Rc, Rc};  // AND_Gate and_39, 8 bits wide
  assign and_40_out = {8{and_13_out[7]}} & {Rc, Rc};  // AND_Gate and_40, 8 bits wide
  assign and_41_out = {8{and_13_out[7]}} & Ra;  // AND_Gate and_41, 8 bits wide
  assign and_42_out = {8{and_14_out[7]}} & Ra;  // AND_Gate and_42, 8 bits wide
  assign and_43_out = {8{and_14_out[7]}} & {Rb, Rb};  // AND_Gate and_43, 8 bits wide
  assign and_44_out = {8{and_15_out[7]}} & {Rb, Rb};  // AND_Gate and_44, 8 bits wide
  assign and_45_out = {8{and_15_out[7]}} & {Rb, Rb};  // AND_Gate and_45, 8 bits wide
  assign and_46_out = {8{and_16_out[7]}} & {Rc, Rc};  // AND_Gate and_46, 8 bits wide
  assign and_47_out = {8{and_16_out[7]}} & {Rc, Rc};  // AND_Gate and_47, 8 bits wide
  not not_1 (not_1_out, OP);
  assign or_2_out = and_28_out | and_29_out | and_30_out;  // OR_Gate or_2, 8 bits wide
  Read_Selector_2 read_selector_2_1 (
    .Need_A_Read(Need_A_Read), .OP(not_1_out), .Ra(Ra), .Rb(Rb), .Rc(Rc), .R1(R1), .R2(R2), .R3(R3),
    .Read1(read_selector_2_1_read1), .Read2(read_selector_2_1_read2));
  assign and_48_out = {8{and_9_out[7]}} & or_2_out;  // AND_Gate and_48, 8 bits wide
  // Probe on read_selector_2_1_read1
  // Probe on read_selector_2_1_read2
  assign Read1 = and_46_out | and_40_out | and_23_out | and_24_out | and_17_out | and_18_out | and_25_out | and_26_out | and_42_out | and_31_out | and_32_out | and_48_out | and_34_out | and_36_out | and_38_out | and_44_out | read_selector_2_1_read1;  // OR_Gate or_3, 8 bits wide
  assign Read2 = read_selector_2_1_read2 | and_43_out | and_27_out | and_33_out | and_35_out | and_37_out | and_39_out | and_41_out | and_45_out | and_47_out;  // OR_Gate or_4, 8 bits wide
endmodule

module Read_Selector_2 (
  input  Need_A_Read,
  input  OP,
  input  [7:0] Ra,
  input  [3:0] Rb,
  input  [3:0] Rc,
  input  [1:0] R1,
  input  [1:0] R2,
  input  [1:0] R3,
  output [7:0] Read1,
  output [7:0] Read2
);

  wire [1:0] subtractor_1_out;
  wire [7:0] and_10_out, and_11_out, and_15_out, and_16_out, and_17_out, and_18_out, and_19_out, and_20_out,
       and_21_out, and_22_out, and_23_out, and_24_out, and_25_out, and_26_out, or_1_out;
  wire [7:7] and_1_out, and_2_out, and_3_out, and_4_out, and_5_out, and_6_out, and_7_out, and_8_out,
       and_9_out, and_12_out, and_13_out, and_14_out;

  Subtractor #(.width(2)) subtractor_1 (.a(R1), .b(R2), .out(subtractor_1_out));  // open: bin, bout
  and and_1 (and_1_out[7], Need_A_Read, ~OP, ~R1[0], ~R1[1], ~R2[1], R2[0]);  // AND_Gate
  and and_2 (and_2_out[7], Need_A_Read, ~OP, ~R1[0], ~R1[1], R2[1], ~R2[0]);  // AND_Gate
  and and_3 (and_3_out[7], Need_A_Read, ~OP, ~R1[1], R1[0], ~R2[1], ~R2[0]);  // AND_Gate
  and and_4 (and_4_out[7], Need_A_Read, ~OP, ~R1[1], R1[0], R2[1], ~R2[0]);  // AND_Gate
  and and_5 (and_5_out[7], Need_A_Read, ~OP, R1[1], ~R1[0], ~R2[1], ~R2[0]);  // AND_Gate
  and and_6 (and_6_out[7], Need_A_Read, ~OP, R1[1], ~R1[0], ~R2[1], R2[0]);  // AND_Gate
  and and_7 (and_7_out[7], Need_A_Read, OP, ~R1[1], ~R1[0], ~R2[1], R2[0], R3[1], ~R3[0]);  // AND_Gate
  and and_8 (and_8_out[7], Need_A_Read, OP, ~R1[1], ~R1[0], R2[1], ~R2[0], ~R3[1], R3[0]);  // AND_Gate
  and and_9 (and_9_out[7], Need_A_Read, ~OP, ~subtractor_1_out[0], ~subtractor_1_out[1]);  // AND_Gate
  assign and_10_out = {8{and_3_out[7]}} & Ra;  // AND_Gate and_10, 8 bits wide
  assign and_11_out = {8{and_4_out[7]}} & {Rc, Rc};  // AND_Gate and_11, 8 bits wide
  and and_12 (and_12_out[7], ~R1[0], ~R1[1]);  // AND_Gate
  and and_13 (and_13_out[7], ~R1[1], R1[0]);  // AND_Gate
  and and_14 (and_14_out[7], R1[1], ~R1[0]);  // AND_Gate
  // Probe on and_15_out
  assign and_15_out = {8{and_1_out[7]}} & {Ra[7:4], Rb};  // AND_Gate and_15, 8 bits wide
  // Probe on and_16_out
  assign and_16_out = {8{and_2_out[7]}} & {Ra[7:4], Rc};  // AND_Gate and_16, 8 bits wide
  // Probe on and_10_out
  // Probe on and_11_out
  // Probe on and_17_out
  assign and_17_out = {8{and_5_out[7]}} & Ra;  // AND_Gate and_17, 8 bits wide
  // Probe on and_18_out
  assign and_18_out = {8{and_6_out[7]}} & {Rb, Rb};  // AND_Gate and_18, 8 bits wide
  assign and_19_out = {8{and_7_out[7]}} & {Rc, Rc};  // AND_Gate and_19, 8 bits wide
  assign and_20_out = {8{and_12_out[7]}} & Ra;  // AND_Gate and_20, 8 bits wide
  assign and_21_out = {8{and_13_out[7]}} & {Rb, Rb};  // AND_Gate and_21, 8 bits wide
  assign and_22_out = {8{and_14_out[7]}} & {Rc, Rc};  // AND_Gate and_22, 8 bits wide
  // Probe on and_23_out
  assign and_23_out = {8{and_7_out[7]}} & {Rb, Rb};  // AND_Gate and_23, 8 bits wide
  // Probe on and_19_out
  assign and_24_out = {8{and_8_out[7]}} & {Rc, Rc};  // AND_Gate and_24, 8 bits wide
  assign and_25_out = {8{and_8_out[7]}} & {Rb, Rb};  // AND_Gate and_25, 8 bits wide
  assign or_1_out = and_20_out | and_21_out | and_22_out;  // OR_Gate or_1, 8 bits wide
  assign and_26_out = {8{and_9_out[7]}} & or_1_out;  // AND_Gate and_26, 8 bits wide
  assign Read1 = and_15_out | and_16_out | and_10_out | and_11_out | and_17_out | and_18_out | and_23_out | and_24_out | and_26_out;  // OR_Gate or_2, 8 bits wide
  // OR_Gate or_3 has open pins: in0=and_19_out, in1=and_25_out, out=open

  assign Read2 = Read1;
endmodule
